// Logisim project n16.circ as structural Verilog: 6 circuits, main circuit main
module main (
  input  IRQ_0,
  input  IRQ_1,
  input  IRQ_2,
  input  IRQ_3,
  input  IRQ_4,
  input  IRQ_5,
  input  IRQ_6,
  input  IRQ_7,
  output [2:0] INT
);

  wire ALU_2, ALU_C, ALU_SRC_A, ALU_Z, CLK, EN_IR, EN_MC_DEC, EN_MDR, EN_PC_0, EN_RAM, MC_DEC_0, MC_DEC_1,
       MC_DEC_2, nCLK, PC_0_SRC, priority_encoder_1_gs, RAM_BYTE, RAM_LD, RAM_W, RU_EN_RT, RU_HI_RS_REG,
       RU_HI_RT_REG, RU_SEL_RS, RU_SEL_RT, RU_SRC, SEL_ALU;
  wire [1:0] ALU_SRC_B, RAM_DAT_SRC;
  wire [2:0] RU_SRC_RS, RU_SRC_RT;
  wire [3:0] ALU_OP;
  wire [7:0] CONTROL_out_10;
  wire [15:0] adder_1_out, ALU_alu_out, ALU_OUT, MDR_q, multiplexer_1_out, multiplexer_2_out,
       multiplexer_3_out, multiplexer_4_out, multiplexer_5_out, PC_0_q, REGISTER_FILE_rs_data_out,
       REGISTER_FILE_rt_data_out, undriven;
  wire [15:10] IR_q;
  wire [31:0] RAM_D_IN, RAM_d_out;

  LED led_1 (.in(CLK));
  Clock clock_1 (.out(CLK));
  not not_1 (nCLK, CLK);
  Adder #(.width(16)) adder_1 (.a(PC_0_q), .b(16'h2), .out(adder_1_out));  // open: cin, cout
  Multiplexer #(.width(16), .enable("false")) multiplexer_1 (
    .in0(adder_1_out), .in1(ALU_OUT), .out(multiplexer_1_out), .sel(PC_0_SRC));
  Register #(.width(16)) PC_0 (.D(multiplexer_1_out), .en(EN_PC_0), .Q(PC_0_q), .clk(nCLK));  // open: clr
  Multiplexer #(.select(2), .width(16), .enable("false")) multiplexer_2 (
    .in0(PC_0_q), .in1(ALU_OUT), .out(multiplexer_2_out), .sel(RAM_DAT_SRC));  // open: in2, in3
  // Probe on RAM_DAT_SRC
  Multiplexer #(.width(16), .enable("false")) multiplexer_3 (
    .in0(ALU_OUT), .out(multiplexer_3_out), .sel(RU_SRC));  // open: in1
  Priority_Encoder priority_encoder_1 (
    .in0(IRQ_0), .in1(IRQ_1), .in2(IRQ_2), .in3(IRQ_3), .in4(IRQ_4), .in5(IRQ_5), .in6(IRQ_6), .in7(IRQ_7),
    .out(INT), .gs(priority_encoder_1_gs));  // open: en_in, en_out
  // Probe on multiplexer_3_out
  // Probe on multiplexer_2_out
  RAM RAM (
    .D_IN(RAM_D_IN), .RAM_W(RAM_W), .CLK(CLK), .ADDR({undriven, multiplexer_2_out}), .RAM_BYTE(RAM_BYTE),
    .SEL(RAM_LD), .D_OUT(RAM_d_out));
  REGISTER_UNIT REGISTER_FILE (
    .RT_DATA_IN(multiplexer_3_out), .SEL_RS(RU_SEL_RS), .EN_RT(RU_EN_RT), .SRC_RT({RU_HI_RT_REG, RU_SRC_RT}),
    .SRC_RS({RU_HI_RS_REG, RU_SRC_RS}), .CLK(CLK), .SEL_RT(RU_SEL_RT),
    .RT_DATA_OUT(REGISTER_FILE_rt_data_out), .RS_DATA_OUT(REGISTER_FILE_rs_data_out));
  // Probe on {RU_HI_RS_REG, RU_SRC_RS}
  // Probe on {RU_HI_RT_REG, RU_SRC_RT}
  // Probe on RAM_d_out[15:0]
  LED led_2 (.in(CLK));
  CONTROL CONTROL (
    .BUS_INST(RAM_d_out[15:10]), .out_10(CONTROL_out_10), .CLK(CLK), .ALU_C(ALU_C), .ALU_Z(ALU_Z),
    .ALU_2(ALU_2), .IRQ(priority_encoder_1_gs), .out_7(EN_MC_DEC), .out_8(MC_DEC_0), .out_9(MC_DEC_1),
    .out_11(MC_DEC_2), .out_12(EN_PC_0), .out_13(PC_0_SRC), .out_14(EN_IR), .EN_PC_0(EN_MDR),
    .out_16(RAM_DAT_SRC[0]), .out_17(RAM_DAT_SRC[1]), .out_18(EN_RAM), .out_19(RAM_W), .out_20(RAM_LD),
    .out_21(RAM_BYTE), .out_22(RU_SRC), .out_23(RU_EN_RT), .out_24(RU_SEL_RT), .out_25(RU_SEL_RS),
    .out_26(RU_HI_RS_REG), .out_27(RU_HI_RT_REG), .out_28(ALU_SRC_A), .out_29(ALU_SRC_B[0]),
    .out_30(ALU_SRC_B[1]), .out_31(SEL_ALU));  // open: out_32, out_33, out_34, out_35, out_36, out_37, out_38, out_39
  // Probe on CONTROL_out_10
  Register #(.width(16)) MDR (.D(RAM_d_out[15:0]), .en(EN_MDR), .Q(MDR_q), .clk(CLK));  // open: clr
  Register #(.width(16)) IR (
    .D(RAM_d_out[15:0]), .en(EN_IR), .Q({IR_q, RU_SRC_RT, RU_SRC_RS, ALU_OP}), .clk(CLK));  // open: clr
  Multiplexer #(.width(16), .enable("false")) multiplexer_4 (
    .in0(REGISTER_FILE_rt_data_out), .in1(PC_0_q), .out(multiplexer_4_out), .sel(ALU_SRC_A));
  Multiplexer #(.select(2), .width(16), .enable("false")) multiplexer_5 (
    .in0(REGISTER_FILE_rs_data_out), .in1(MDR_q), .out(multiplexer_5_out), .sel(ALU_SRC_B));  // open: in2, in3
  LED led_3 (.in(EN_MC_DEC));
  LED led_4 (.in(MC_DEC_0));
  LED led_5 (.in(MC_DEC_1));
  LED led_6 (.in(MC_DEC_2));
  LED led_7 (.in(EN_PC_0));
  LED led_8 (.in(PC_0_SRC));
  LED led_9 (.in(EN_IR));
  LED led_10 (.in(EN_MDR));
  // Probe on RAM_DAT_SRC
  LED led_11 (.in(EN_RAM));
  LED led_12 (.in(RAM_W));
  LED led_13 (.in(RAM_LD));
  LED led_14 (.in(RAM_BYTE));
  LED led_15 (.in(RU_SRC));
  LED led_16 (.in(RU_EN_RT));
  LED led_17 (.in(RU_SEL_RT));
  LED led_18 (.in(RU_SEL_RS));
  LED led_19 (.in(RU_HI_RS_REG));
  LED led_20 (.in(RU_HI_RT_REG));
  LED led_21 (.in(ALU_SRC_A));
  // Probe on ALU_SRC_B
  LED led_22 (.in(SEL_ALU));
  // Probe on multiplexer_4_out
  // Probe on multiplexer_5_out
  // Probe on ALU_alu_out
  ALU ALU (
    .R_S(multiplexer_4_out), .R_T(multiplexer_5_out), .ALU_OP(ALU_OP), .SEL_ALU(SEL_ALU),
    .ALU_OUT(ALU_alu_out), .Z(ALU_Z), .C(ALU_C), .N(ALU_2));
  // Probe on ALU_OP
  Register #(.width(16)) u_ALU_OUT (.D(ALU_alu_out), .Q(ALU_OUT), .clk(CLK));  // open: en, clr

  // Other names for the same wires on the sheet: RU_SRC_RS[3] = RU_HI_RS_REG; RU_SRC_RT[3] = RU_HI_RT_REG
endmodule

module RAM (
  input  [31:0] D_IN,
  input  RAM_W,
  input  CLK,
  input  [31:0] ADDR,
  input  RAM_BYTE,
  input  SEL,
  output [31:0] D_OUT
);

  wire and_1_out, and_2_out, decoder_1_out0, decoder_1_out1, not_1_out, not_2_out;
  wire [7:0] demultiplexer_1_out0, multiplexer_1_out;
  wire [31:0] multiplexer_2_out;
  wire [31:8] demultiplexer_1_out1, undriven;

  LED led_1 (.in(CLK));
  Pull_Resistor pull_resistor_1 (.node(ADDR));
  not not_1 (not_1_out, RAM_BYTE);
  Decoder decoder_1 (.out0(decoder_1_out0), .out1(decoder_1_out1), .sel(ADDR[0]), .en(RAM_BYTE));
  and and_1 (and_1_out, not_1_out, RAM_W);
  not not_2 (not_2_out, RAM_W);
  Demultiplexer #(.width(8)) demultiplexer_1 (
    .out0(demultiplexer_1_out0), .out1(demultiplexer_1_out1[15:8]), .in(D_IN[7:0]), .sel(ADDR[0]),
    .en(and_2_out));
  and and_2 (and_2_out, RAM_BYTE, RAM_W);
  Pull_Resistor #(.pull(1)) pull_resistor_2 (.node(decoder_1_out0));
  Pull_Resistor #(.pull(1)) pull_resistor_3 (.node(decoder_1_out1));
  assign {demultiplexer_1_out1, demultiplexer_1_out0} = and_1_out ? D_IN : 32'bz;  // Controlled_Buffer controlled_buffer_1
  ROM #(.addrWidth(24)) rom_1 (.addr(ADDR[24:1]), .data(demultiplexer_1_out0), .sel(decoder_1_out0));
  ROM #(.addrWidth(24)) rom_2 (.addr(ADDR[24:1]), .data(demultiplexer_1_out1[15:8]), .sel(decoder_1_out1));
  Multiplexer #(.width(8), .enable("false")) multiplexer_1 (
    .in0(demultiplexer_1_out0), .in1(demultiplexer_1_out1[15:8]), .out(multiplexer_1_out));  // open: sel
  Multiplexer #(.width(32), .enable("false")) multiplexer_2 (
    .in0({demultiplexer_1_out1, demultiplexer_1_out0}), .in1({undriven, multiplexer_1_out}),
    .out(multiplexer_2_out), .sel(RAM_BYTE));
  assign D_OUT = SEL ? multiplexer_2_out : 32'bz;  // Controlled_Buffer controlled_buffer_2
  LED led_2 (.in(CLK));

  // Notes on the sheet:
  //   contents of rom_1 (hex, n*v repeats v):
  //   11 22 33 44 55 66
  //   contents of rom_2 (hex, n*v repeats v):
  //   a0 b0 c0 d0 e0 f0 a0 b0 c0 d0 e0 f0 a0 b0 c0 d0 e0 f0 a0 b0 c0 d0 e0 f0 a0 b0 c0 d0 e0 f0 a0 b0 c0
  //   d0 e0 f0 a0 b0 c0 d0 e0 f0 a0 b0 c0 d0 e0 f0 a0 b0 c0 d0 e0 f0 a0 b0 c0 d0 e0 f0 a0 b0 c0 d0 e0 f0
  //   a0 b0 c0 d0 e0 f0 a0 b0 c0 d0 e0 f0 a0 b0 c0 d0 e0 f0 a0 b0 c0 d0 e0 f0 a0 b0 c0 d0 e0 f0 a0 b0 c0
  //   d0 e0 f0 a0 b0 c0 d0 e0 f0 a0 b0 c0 d0 e0 f0 a0 b0 c0 d0 e0 f0 a0 b0 c0 d0 e0 f0 a0 b0 c0 d0 e0 f0
  //   a0 b0 c0 d0 e0 f0 a0 b0 c0 d0 e0 f0 a0 b0 c0 d0 e0 f0 a0 b0 c0 d0 e0 f0 a0 b0 c0 d0 e0 f0 a0 b0 c0
  //   d0 e0 f0 a0 b0 c0 d0 e0 f0 a0 b0 c0 d0 e0 f0 a0 b0 c0 d0 e0 f0 a0 b0 c0 d0 e0 f0 a0 b0 c0 d0 e0 f0
  //   a0 b0 c0 d0 e0 f0 a0 b0 c0 d0 e0 f0 a0 b0 c0 d0 e0 f0 a0 b0 c0 d0 e0 f0 a0 b0 c0 d0 e0 f0 a0 b0 c0
  //   d0 e0 f0 a0 b0 c0 d0 e0 f0 a0 b0 c0 d0 e0 f0 a0 b0 c0 d0 e0 f0 a0 b0 c0 d0 e0 f0 a0 b0 c0 d0 e0 f0
  //   a0 b0 c0 d0 e0 f0 a0 b0 c0 d0 e0 f0 a0 b0 c0 d0 e0 f0 a0 b0 c0 d0 e0 f0 a0 b0 c0 d0 e0 f0 a0 b0 c0
  //   d0 e0 f0 a0 b0 c0 d0 e0 f0 a0 b0 c0 d0 e0 f0 a0 b0 c0 d0 e0 f0 a0 b0 c0 d0 e0 f0 a0 b0 c0 d0 e0 f0
  //   a0 b0 c0 d0 e0 f0 a0 b0 c0 d0 e0 f0 a0 b0 c0 d0 e0 f0 a0 b0 c0 d0 e0 f0 a0 b0 c0 d0 e0 f0 a0 b0 c0
  //   d0 e0 f0 a0 b0 c0 d0 e0 f0 a0 b0 c0 d0 e0 f0 a0 b0 c0 d0 e0 f0 a0 b0 c0 d0 e0 f0 a0 b0 c0 d0 e0 f0
  //   a0 b0 c0 d0 e0 f0 a0 b0 c0 d0 e0 f0 a0 b0 c0 d0 e0 f0 a0 b0 c0 d0 e0 f0 a0 b0 c0 d0 e0 f0 a0 b0 c0
  //   d0 e0 f0 a0 b0 c0 d0 e0 f0 a0 b0 c0 d0 e0 f0 a0 b0 c0 d0 e0 f0 a0 b0 c0 d0 e0 f0 a0 b0 c0 d0 e0 f0
  //   a0 b0 c0 d0 e0 f0 a0 b0 c0 d0 e0 f0 a0 b0 c0 d0 e0 f0 a0 b0 c0 d0 e0 f0 a0 b0 c0 d0 e0 f0 a0 b0 c0
  //   d0 e0 f0 a0 b0 c0 d0 e0 f0 a0 b0 c0 d0 e0 f0 a0 b0 c0 d0 e0 f0 a0 b0 c0 d0 e0 f0 a0 b0 c0 d0 e0 f0
  //   a0 b0 c0 d0 e0 f0 a0 b0 c0 d0 e0 f0 a0 b0 c0 d0 e0 f0 a0 b0 c0 d0 e0 f0 a0 b0 c0 d0 e0 f0 a0 b0 c0
  //   d0 e0 f0 a0 b0 c0 d0 e0 f0 a0 b0 c0 d0 e0 f0 a0 b0 c0 d0 e0 f0 a0 b0 c0 d0 e0 f0 a0 b0 c0 d0 e0 f0
  //   a0 b0 c0 d0 e0 f0 a0 b0 c0 d0 e0 f0 a0 b0 c0 d0 e0 f0 a0 b0 c0 d0 e0 f0 a0 b0 c0 d0 e0 f0 a0 b0 c0
  //   d0 e0 f0 a0 b0 c0 d0 e0 f0 a0 b0 c0 d0 e0 f0 a0 b0 c0 d0 e0 f0 a0 b0 c0 d0 e0 f0 a0 b0 c0 d0 e0 f0
  //   a0 b0 c0 d0 e0 f0 a0 b0 c0 d0 e0 f0 a0 b0 c0 d0 e0 f0 a0 b0 c0 d0 e0 f0 a0 b0 c0 d0 e0 f0 a0 b0 c0
  //   d0 e0 f0 a0 b0 c0 d0 e0 f0 a0 b0 c0 d0 e0 f0 a0 b0 c0 d0 e0 f0 a0 b0 c0 d0 e0 f0 a0 b0 c0 d0 e0 f0
  //   a0 b0 c0 d0 e0 f0 a0 b0 c0 d0 e0 f0 a0 b0 c0 d0 e0 f0 a0 b0 c0 d0 e0 f0 a0 b0 c0 d0 e0 f0 a0 b0 c0
  //   d0 e0 f0 a0 b0 c0 d0 e0 f0 a0 b0 c0 d0 e0 f0 a0 b0 c0 d0 e0 f0 a0 b0 c0 d0 e0 f0 a0 b0 c0 d0 e0 f0
  //   a0 b0 c0 d0 e0 f0 a0 b0 c0 d0 e0 f0 a0 b0 c0 d0 e0 f0 a0 b0 c0 d0 e0 f0 a0 b0 c0 d0 e0 f0 a0 b0 c0
  //   d0 e0 f0 a0 b0 c0 d0 e0 f0 a0 b0 c0 d0 e0 f0 a0 b0 c0 d0 e0 f0 a0 b0 c0 d0 e0 f0 a0 b0 c0 d0 e0 f0
  //   a0 b0 c0 d0 e0 f0 a0 b0 c0 d0 e0 f0 a0 b0 c0 d0 e0 f0 a0 b0 c0 d0 e0 f0 a0 b0 c0 d0 e0 f0 a0 b0 c0
  //   d0 e0 f0 a0 b0 c0 d0 e0 f0 a0 b0 c0 d0 e0 f0 a0 b0 c0 d0 e0 f0 a0 b0 c0 d0 e0 f0 a0 b0 c0 d0 e0 f0
  //   a0 b0 c0 d0 e0 f0 a0 b0 c0 d0 e0 f0 a0 b0 c0 d0 e0 f0 a0 b0 c0 d0 e0 f0 a0 b0 c0 d0 e0 f0 a0 b0 c0
  //   d0 e0 f0 a0 b0 c0 d0 e0 f0 a0 b0 c0 d0 e0 f0 a0 b0 c0 d0 e0 f0 a0 b0 c0 d0 e0 f0 a0 b0 c0 d0 e0 f0
  //   a0 b0 c0 d0 e0 f0 a0 b0 c0 d0 e0 f0 a0 b0 c0 d0 e0 f0 a0 b0 c0 d0 e0 f0 a0 b0 c0 d0 e0 f0 a0 b0 c0
  //   d0 e0 f0 a0 b0 c0 d0 e0 f0 a0 b0 c0 d0 e0 f0 a0 b0 c0 d0 e0 f0 a0 b0 c0 d0 e0 f0 a0 b0 c0 d0 e0 f0
  //   a0 b0 c0 d0 e0 f0 a0 b0 c0 d0 e0 f0 a0 b0 c0 d0 e0 f0 a0 b0 c0 d0 e0 f0 a0 b0 c0 d0 e0 f0 a0 b0 c0
  //   d0 e0 f0 a0 b0 c0 d0 e0 f0 a0 b0 c0 d0 e0 f0 a0 b0 c0 d0 e0 f0 a0 b0 c0 d0 e0 f0 a0 b0 c0 d0 e0 f0
  //   a0 b0 c0 d0 e0 f0 a0 b0 c0 d0 e0 f0 a0 b0 c0 d0 e0 f0 a0 b0 c0 d0 e0 f0 a0 b0 c0 d0 e0 f0 a0 b0 c0
  //   d0 e0 f0 a0 b0 c0 d0 e0 f0 a0 b0 c0 d0 e0 f0 a0 b0 c0 d0 e0 f0 a0 b0 c0 d0 e0 f0 a0 b0 c0 d0 e0 f0
  //   a0 b0 c0 d0 e0 f0 a0 b0 c0 d0 e0 f0 a0 b0 c0 d0 e0 f0 a0 b0 c0 d0 e0 f0 a0 b0 c0 d0 e0 f0 a0 b0 c0
  //   d0 e0 f0 a0 b0 c0 d0 e0 f0 a0 b0 c0 d0 e0 f0 a0 b0 c0 d0 e0 f0 a0 b0 c0 d0 e0 f0 a0 b0 c0 d0 e0 f0
  //   a0 b0 c0 d0 e0 f0 a0 b0 c0 d0 e0 f0 a0 b0 c0 d0 e0 f0 a0 b0 c0 d0 e0 f0 a0 b0 c0 d0 e0 f0 a0 b0 c0
  //   d0 e0 f0 a0 b0 c0 d0 e0 f0 a0 b0 c0 d0 e0 f0 a0 b0 c0 d0 e0 f0 a0 b0 c0 d0 e0 f0 a0 b0 c0 d0 e0 f0
  //   a0 b0 c0 d0 e0 f0 a0 b0 c0 d0 e0 f0 a0 b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
endmodule

module CONTROL (
  input  [5:0] BUS_INST,
  input  CLK,
  input  ALU_C,
  input  ALU_Z,
  input  ALU_2,
  input  IRQ,
  output out_7,
  output out_8,
  output out_9,
  output [7:0] out_10,
  output out_11,
  output out_12,
  output out_13,
  output out_14,
  output EN_PC_0,
  output out_16,
  output out_17,
  output out_18,
  output out_19,
  output out_20,
  output out_21,
  output out_22,
  output out_23,
  output out_24,
  output out_25,
  output out_26,
  output out_27,
  output out_28,
  output out_29,
  output out_30,
  output out_31,
  output out_32,
  output out_33,
  output out_34,
  output out_35,
  output out_36,
  output out_37,
  output out_38,
  output out_39
);

  wire and_1_out, and_2_out, multiplexer_1_out, nCLK, not_2_out, not_3_out;
  wire [4:4] rom_1_data;
  wire [7:0] BUS_INST_t;

  not not_1 (nCLK, CLK);
  assign BUS_INST_t = not_2_out ? {BUS_INST, 2'b00} : 8'bz;  // Controlled_Buffer controlled_buffer_1
  not not_2 (not_2_out, out_7);
  Multiplexer #(.select(3), .enable("false")) multiplexer_1 (
    .in0(1'b1), .in1(ALU_C), .in2(ALU_Z), .in3(ALU_2), .in4(IRQ), .out(multiplexer_1_out),
    .sel({out_11, out_9, out_8}));  // open: in5, in6, in7
  LED led_1 (.in(CLK));
  Register register_1 (.D(BUS_INST_t), .Q(out_10), .clk(nCLK));  // open: en, clr
  and and_1 (and_1_out, multiplexer_1_out, out_7);
  and and_2 (and_2_out, not_3_out, out_7);
  not not_3 (not_3_out, multiplexer_1_out);
  ROM rom_1 (.addr(out_10), .data({EN_PC_0, out_14, out_13, rom_1_data[4], out_11, out_9, out_8, out_7}));  // open: sel
  ROM rom_2 (.addr(out_10), .data({out_23, out_22, out_21, out_20, out_19, out_18, out_17, out_16}));  // open: sel
  ROM rom_3 (.addr(out_10), .data({out_31, out_30, out_29, out_28, out_27, out_26, out_25, out_24}));  // open: sel
  ROM rom_4 (.addr(out_10), .data({out_39, out_38, out_37, out_36, out_35, out_34, out_33, out_32}));  // open: sel
  ROM rom_5 (.addr(out_10), .data(BUS_INST_t), .sel(and_1_out));
  ROM rom_6 (.addr(out_10), .data(BUS_INST_t), .sel(and_2_out));
  D_Flip_Flop d_ff_1 (.clk(CLK), .D(rom_1_data[4]), .Q(out_12));  // open: Qn, preset, en, reset

  // Other names for the same wires on the sheet: EN_MC_DEC = out_7; MC_DEC_0 = out_8; MC_DEC_1 = out_9;
  //   MC_DEC_2 = out_11

  // Notes on the sheet:
  //   contents of rom_1 (hex, n*v repeats v):
  //   d0 d0 0 0 0 0 0 0 0 0 0 0 0 0 0 0 0 0 0 0 0 0 0 0 0 0 0 0 0 0 0 0 0 0 0 0 0 0 0 0 0 0 0 0 0 0 0 0 0
  //   0 0 0 0 0 0 0 0 0 0 0 0 0 0 0 0 0 0 0 0 0 0 0 0 0 0 0 0 0 0 0 0 0 0 0 0 0 0 0 0 0 0 0 0 0 0 0 0 0 0
  //   0 0 0 0 0 0 0 0 0 0 0 0 0 0 0 0 0 0 0 0 0 0 0 0 0 0 0 0 0 0 0 0 0 0 0 0 0 0 0 0 0 0 0 0 0 0 0 0 0 0
  //   0 0 0 0 0 0 0 0 0 0 0 d0 0 0 0 0 0 0 0 0 0 0 0 0 0 0 0 50 0 0 0 0 0 0 0 0 0 0 0 0 0 0 0 50 0 0 0 0 0
  //   0 0 0 0 0 0 0 0 0 0 50 0 0 0 0 0 0 0 0 0 0 0 0 0 0 0 50 0 0 0 0 0 0 0 0 0 0 0 0 0 0 0 50 0 0 0 0 0 0
  //   0 0 0 0 0 0 0 0 0
  //   contents of rom_2 (hex, n*v repeats v):
  //   10 10 0 0 0 0 0 0 0 0 0 0 0 0 0 0 0 0 0 0 0 0 0 0 0 0 0 0 0 0 0 0 0 0 0 0 0 0 0 0 0 0 0 0 0 0 0 0 0
  //   0 0 0 0 0 0 0 0 0 0 0 0 0 0 0 0 0 0 0 0 0 0 0 0 0 0 0 0 0 0 0 0 0 0 0 0 0 0 0 0 0 0 0 0 0 0 0 0 0 0
  //   0 0 0 0 0 0 0 0 0 0 0 0 0 0 0 0 0 0 0 0 0 0 0 0 0 0 0 0 0 0 0 0 0 0 0 0 0 0 0 0 0 0 0 0 0 0 0 0 0 0
  //   0 0 0 0 0 0 0 0 0 0 0 50 0 0 0 0 0 0 0 0 0 0 0 0 0 0 0 90 0 0 0 0 0 0 0 0 0 0 0 0 0 0 0 10 0 0 0 0 0
  //   0 0 0 0 0 0 0 0 0 0 10 0 0 0 0 0 0 0 0 0 0 0 0 0 0 0 90 0 0 0 0 0 0 0 0 0 0 0 0 0 0 0 10 0 0 0 0 0 0
  //   0 0 0 0 0 0 0 0 0
  //   contents of rom_3 (hex, n*v repeats v):
  //   0 0 0 0 0 0 0 0 0 0 0 0 0 0 0 0 0 0 0 0 0 0 0 0 0 0 0 0 0 0 0 0 0 0 0 0 0 0 0 0 0 0 0 0 0 0 0 0 0 0
  //   0 0 0 0 0 0 0 0 0 0 0 0 0 0 0 0 0 0 0 0 0 0 0 0 0 0 0 0 0 0 0 0 0 0 0 0 0 0 0 0 0 0 0 0 0 0 0 0 0 0
  //   0 0 0 0 0 0 0 0 0 0 0 0 0 0 0 0 0 0 0 0 0 0 0 0 0 0 0 0 0 0 0 0 0 0 0 0 0 0 0 0 0 0 0 0 0 0 0 0 0 0
  //   0 0 0 0 0 0 0 0 0 0 0 0 0 0 0 0 0 0 0 0 0 0 0 0 0 0 0 0 0 0 0 0 0 0 0 0 0 0 0 0 0 0 1 0 0 0 0 0 0 0
  //   0 0 0 0 0 0 0 0 2 0 0 0 0 0 0 0 0 0 0 0 0 0 0 0 0 0 0 0 0 0 0 0 0 0 0 0 0 0 0 0 80 0 0 0 0 0 0 0 0 0
  //   0 0 0 0 0 0
  //   contents of rom_4 (hex, n*v repeats v):
  //   1 2 0 0 0 0 0 0 0 0 0 0 0 0 0 0 0 0 0 0 0 0 0 0 0 0 0 0 0 0 0 0 0 0 0 0 0 0 0 0 0 0 0 0 0 0 0 0 0 0
  //   0 0 0 0 0 0 0 0 0 0 0 0 0 0 0 0 0 0 0 0 0 0 0 0 0 0 0 0 0 0 0 0 0 0 0 0 0 0 0 0 0 0 0 0 0 0 0 0 0 0
  //   0 0 0 0 0 0 0 0 0 0 0 0 0 0 0 0 0 0 0 0 0 0 0 0 0 0 0 0 0 0 0 0 0 0 0 0 0 0 0 0 0 0 0 0 0 0 0 0 0 0
  //   0 0 0 0 0 0 0 0 0 0 a1 0 0 0 0 0 0 0 0 0 0 0 0 0 0 0 b1 0 0 0 0 0 0 0 0 0 0 0 0 0 0 0 c1 0 0 0 0 0 0
  //   0 0 0 0 0 0 0 0 0 d1 0 0 0 0 0 0 0 0 0 0 0 0 0 0 0 e1 0 0 0 0 0 0 0 0 0 0 0 0 0 0 0 f1 0 0 0 0 0 0 0
  //   0 0 0 0 0 0 0 0
  //   contents of rom_5 (hex, n*v repeats v):
  //   0 0 0 0 0 0 0 0 0 0 0 0 0 0 0 0 0 0 0 0 0 0 0 0 0 0 0 0 0 0 0 0 0 0 0 0 0 0 0 0 0 0 0 0 0 0 0 0 0 0
  //   0 0 0 0 0 0 0 0 0 0 0 0 0 0 0 0 0 0 0 0 0 0 0 0 0 0 0 0 0 0 0 0 0 0 0 0 0 0 0 0 0 0 0 0 0 0 0 0 0 0
  //   0 0 0 0 0 0 0 0 0 0 0 0 0 0 0 0 0 0 0 0 0 0 0 0 0 0 0 0 0 0 0 0 0 0 0 0 0 0 0 0 0 0 0 0 0 0 0 0 0 0
  //   0 0 0 0 0 0 0 0 0 0 0 0 0 0 0 0 0 0 0 0 0 0 0 0 0 0 0 0 0 0 0 0 0 0 0 0 0 0 0 0 0 0 0 0 0 0 0 0 0 0
  //   0 0 0 0 0 0 0 0 0 0 0 0 0 0 0 0 0 0 0 0 0 0 0 0 0 0 0 0 0 0 0 0 0 0 0 0 0 0 0 0 0 0 0 0 0 0 0 0 0 0
  //   0 0 0 0 0 0
  //   contents of rom_6 (hex, n*v repeats v):
  //   0 0 0 0 0 0 0 0 0 0 0 0 0 0 0 0 0 0 0 0 0 0 0 0 0 0 0 0 0 0 0 0 0 0 0 0 0 0 0 0 0 0 0 0 0 0 0 0 0 0
  //   0 0 0 0 0 0 0 0 0 0 0 0 0 0 0 0 0 0 0 0 0 0 0 0 0 0 0 0 0 0 0 0 0 0 0 0 0 0 0 0 0 0 0 0 0 0 0 0 0 0
  //   0 0 0 0 0 0 0 0 0 0 0 0 0 0 0 0 0 0 0 0 0 0 0 0 0 0 0 0 0 0 0 0 0 0 0 0 0 0 0 0 0 0 0 0 0 0 0 0 0 0
  //   0 0 0 0 0 0 0 0 0 0 0 0 0 0 0 0 0 0 0 0 0 0 0 0 0 0 0 0 0 0 0 0 0 0 0 0 0 0 0 0 0 0 0 0 0 0 0 0 0 0
  //   0 0 0 0 0 0 0 0 0 0 0 0 0 0 0 0 0 0 0 0 0 0 0 0 0 0 0 0 0 0 0 0 0 0 0 0 0 0 0 0 0 0 0 0 0 0 0 0 0 0
  //   0 0 0 0 0 0
endmodule

module _3_STATE_REGISTER (
  input  [15:0] D,
  input  sel_s,
  input  en,
  input  clk,
  input  _0,
  input  sel_t,
  output [15:0] Q_S,
  output [15:0] Q_T
);

  wire [15:0] register_1_q;

  Register #(.width(16)) register_1 (.D(D), .en(en), .Q(register_1_q), .clk(clk), .clr(_0));
  assign Q_S = sel_s ? register_1_q : 16'bz;  // Controlled_Buffer controlled_buffer_1
  Pull_Resistor pull_resistor_1 (.node(sel_s));
  assign Q_T = sel_t ? register_1_q : 16'bz;  // Controlled_Buffer controlled_buffer_2
  Pull_Resistor pull_resistor_2 (.node(sel_t));
endmodule

module REGISTER_UNIT (
  input  [15:0] RT_DATA_IN,
  input  EN_RT,
  input  SEL_RT,
  input  [3:0] SRC_RT,
  input  CLK,
  input  [3:0] SRC_RS,
  input  SEL_RS,
  output [15:0] RT_DATA_OUT,
  output [15:0] RS_DATA_OUT
);

  wire decoder_1_out0, decoder_1_out1, decoder_1_out2, decoder_1_out3, decoder_1_out4, decoder_1_out5,
       decoder_1_out6, decoder_1_out7, decoder_1_out8, decoder_1_out9, decoder_1_out10, decoder_1_out11,
       decoder_1_out12, decoder_1_out13, decoder_1_out14, decoder_1_out15, decoder_2_out0, decoder_2_out1,
       decoder_2_out2, decoder_2_out3, decoder_2_out4, decoder_2_out5, decoder_2_out6, decoder_2_out7,
       decoder_2_out8, decoder_2_out9, decoder_2_out10, decoder_2_out11, decoder_2_out12, decoder_2_out13,
       decoder_2_out14, decoder_2_out15, decoder_3_out0, decoder_3_out1, decoder_3_out2, decoder_3_out3,
       decoder_3_out4, decoder_3_out5, decoder_3_out6, decoder_3_out7, decoder_3_out8, decoder_3_out9,
       decoder_3_out10, decoder_3_out11, decoder_3_out12, decoder_3_out13, decoder_3_out14, decoder_3_out15;

  Decoder #(.select(4)) decoder_1 (
    .out0(decoder_1_out0), .out1(decoder_1_out1), .out2(decoder_1_out2), .out3(decoder_1_out3),
    .out4(decoder_1_out4), .out5(decoder_1_out5), .out6(decoder_1_out6), .out7(decoder_1_out7),
    .out8(decoder_1_out8), .out9(decoder_1_out9), .out10(decoder_1_out10), .out11(decoder_1_out11),
    .out12(decoder_1_out12), .out13(decoder_1_out13), .out14(decoder_1_out14), .out15(decoder_1_out15),
    .sel(SRC_RT), .en(EN_RT));
  Decoder #(.select(4)) decoder_2 (
    .out0(decoder_2_out0), .out1(decoder_2_out1), .out2(decoder_2_out2), .out3(decoder_2_out3),
    .out4(decoder_2_out4), .out5(decoder_2_out5), .out6(decoder_2_out6), .out7(decoder_2_out7),
    .out8(decoder_2_out8), .out9(decoder_2_out9), .out10(decoder_2_out10), .out11(decoder_2_out11),
    .out12(decoder_2_out12), .out13(decoder_2_out13), .out14(decoder_2_out14), .out15(decoder_2_out15),
    .sel(SRC_RS), .en(SEL_RS));
  _3_STATE_REGISTER u_3_state_register_1 (
    .D(RT_DATA_IN), .en(decoder_1_out0), .clk(CLK), .sel_s(decoder_2_out0), .sel_t(decoder_3_out0),
    .Q_S(RS_DATA_OUT), .Q_T(RT_DATA_OUT));  // open: _0
  _3_STATE_REGISTER u_3_state_register_2 (
    .D(RT_DATA_IN), .en(decoder_1_out4), .clk(CLK), .sel_s(decoder_2_out4), .sel_t(decoder_3_out4),
    .Q_S(RS_DATA_OUT), .Q_T(RT_DATA_OUT));  // open: _0
  _3_STATE_REGISTER u_3_state_register_3 (
    .D(RT_DATA_IN), .en(decoder_1_out8), .clk(CLK), .sel_s(decoder_2_out8), .sel_t(decoder_3_out8),
    .Q_S(RS_DATA_OUT), .Q_T(RT_DATA_OUT));  // open: _0
  _3_STATE_REGISTER u_3_state_register_4 (
    .D(RT_DATA_IN), .en(decoder_1_out12), .clk(CLK), .sel_s(decoder_2_out12), .sel_t(decoder_3_out12),
    .Q_S(RS_DATA_OUT), .Q_T(RT_DATA_OUT));  // open: _0
  _3_STATE_REGISTER u_3_state_register_5 (
    .D(RT_DATA_IN), .en(decoder_1_out1), .clk(CLK), .sel_s(decoder_2_out1), .sel_t(decoder_3_out1),
    .Q_S(RS_DATA_OUT), .Q_T(RT_DATA_OUT));  // open: _0
  _3_STATE_REGISTER u_3_state_register_6 (
    .D(RT_DATA_IN), .en(decoder_1_out5), .clk(CLK), .sel_s(decoder_2_out5), .sel_t(decoder_3_out5),
    .Q_S(RS_DATA_OUT), .Q_T(RT_DATA_OUT));  // open: _0
  _3_STATE_REGISTER u_3_state_register_7 (
    .D(RT_DATA_IN), .en(decoder_1_out9), .clk(CLK), .sel_s(decoder_2_out9), .sel_t(decoder_3_out9),
    .Q_S(RS_DATA_OUT), .Q_T(RT_DATA_OUT));  // open: _0
  _3_STATE_REGISTER u_3_state_register_8 (
    .D(RT_DATA_IN), .en(decoder_1_out13), .clk(CLK), .sel_s(decoder_2_out13), .sel_t(decoder_3_out13),
    .Q_S(RS_DATA_OUT), .Q_T(RT_DATA_OUT));  // open: _0
  _3_STATE_REGISTER u_3_state_register_9 (
    .D(RT_DATA_IN), .en(decoder_1_out2), .clk(CLK), .sel_s(decoder_2_out2), .sel_t(decoder_3_out2),
    .Q_S(RS_DATA_OUT), .Q_T(RT_DATA_OUT));  // open: _0
  _3_STATE_REGISTER u_3_state_register_10 (
    .D(RT_DATA_IN), .en(decoder_1_out6), .clk(CLK), .sel_s(decoder_2_out6), .sel_t(decoder_3_out6),
    .Q_S(RS_DATA_OUT), .Q_T(RT_DATA_OUT));  // open: _0
  _3_STATE_REGISTER u_3_state_register_11 (
    .D(RT_DATA_IN), .en(decoder_1_out10), .clk(CLK), .sel_s(decoder_2_out10), .sel_t(decoder_3_out10),
    .Q_S(RS_DATA_OUT), .Q_T(RT_DATA_OUT));  // open: _0
  _3_STATE_REGISTER u_3_state_register_12 (
    .D(RT_DATA_IN), .en(decoder_1_out14), .clk(CLK), .sel_s(decoder_2_out14), .sel_t(decoder_3_out14),
    .Q_S(RS_DATA_OUT), .Q_T(RT_DATA_OUT));  // open: _0
  _3_STATE_REGISTER u_3_state_register_13 (
    .D(RT_DATA_IN), .en(decoder_1_out3), .clk(CLK), .sel_s(decoder_2_out3), .sel_t(decoder_3_out3),
    .Q_S(RS_DATA_OUT), .Q_T(RT_DATA_OUT));  // open: _0
  _3_STATE_REGISTER u_3_state_register_14 (
    .D(RT_DATA_IN), .en(decoder_1_out7), .clk(CLK), .sel_s(decoder_2_out7), .sel_t(decoder_3_out7),
    .Q_S(RS_DATA_OUT), .Q_T(RT_DATA_OUT));  // open: _0
  _3_STATE_REGISTER u_3_state_register_15 (
    .D(RT_DATA_IN), .en(decoder_1_out11), .clk(CLK), .sel_s(decoder_2_out11), .sel_t(decoder_3_out11),
    .Q_S(RS_DATA_OUT), .Q_T(RT_DATA_OUT));  // open: _0
  _3_STATE_REGISTER u_3_state_register_16 (
    .D(RT_DATA_IN), .en(decoder_1_out15), .clk(CLK), .sel_s(decoder_2_out15), .sel_t(decoder_3_out15),
    .Q_S(RS_DATA_OUT), .Q_T(RT_DATA_OUT));  // open: _0
  Decoder #(.select(4)) decoder_3 (
    .out0(decoder_3_out0), .out1(decoder_3_out1), .out2(decoder_3_out2), .out3(decoder_3_out3),
    .out4(decoder_3_out4), .out5(decoder_3_out5), .out6(decoder_3_out6), .out7(decoder_3_out7),
    .out8(decoder_3_out8), .out9(decoder_3_out9), .out10(decoder_3_out10), .out11(decoder_3_out11),
    .out12(decoder_3_out12), .out13(decoder_3_out13), .out14(decoder_3_out14), .out15(decoder_3_out15),
    .sel(SRC_RT), .en(SEL_RT));
endmodule

module ALU (
  input  [15:0] R_S,
  input  [15:0] R_T,
  input  [3:0] ALU_OP,
  input  SEL_ALU,
  output [15:0] ALU_OUT,
  output Z,
  output C,
  output N
);

  wire clock_1_out;
  wire [15:0] adder_1_out, and_1_out, divider_1_out, multiplier_1_out, or_1_out, subtractor_1_out;

  LED led_1 (.in(clock_1_out));
  Clock clock_1 (.out(clock_1_out));
  Pull_Resistor pull_resistor_1 (.node(R_S));
  Pull_Resistor pull_resistor_2 (.node(R_T));
  Adder #(.width(16)) adder_1 (.a(R_S), .b(R_T), .out(adder_1_out));  // open: cin, cout
  Subtractor #(.width(16)) subtractor_1 (.a(R_S), .b(R_T), .out(subtractor_1_out));  // open: bin, bout
  Multiplier #(.width(16)) multiplier_1 (.a(R_S), .b(R_T), .out(multiplier_1_out));  // open: cin, cout
  Divider #(.width(16)) divider_1 (.a(R_S), .b(R_T), .out(divider_1_out));  // open: upper, rem
  assign or_1_out = R_S | R_T;  // OR_Gate or_1, 16 bits wide
  assign and_1_out = R_S & R_T;  // AND_Gate and_1, 16 bits wide
  Multiplexer #(.select(4), .width(16)) multiplexer_1 (
    .in0(R_S), .in1(adder_1_out), .in2(subtractor_1_out), .in3(multiplier_1_out), .in4(divider_1_out),
    .in5(or_1_out), .in6(and_1_out), .out(ALU_OUT), .sel(ALU_OP), .en(SEL_ALU));  // open: in7, in8, in9, in10, in11, in12, in13, in14, in15
  Pull_Resistor pull_resistor_3 (.node(C));

  assign N = C;
  assign Z = C;
endmodule
